// Logisim project 02-bcdadder.circ as structural Verilog
module BCDshow (
  input  E,
  input  D,
  input  C,
  input  B,
  input  A,
  output a4,
  output a3,
  output a2,
  output a1,
  output a0
);

  wire and_1_out, and_2_out, and_3_out, and_4_out, and_5_out, and_6_out, and_7_out, and_8_out, and_9_out,
       and_10_out, not_1_out, not_2_out, not_3_out, not_4_out, not_5_out, not_6_out, not_7_out, not_8_out;

  and and_1 (and_1_out, D, B);
  and and_2 (and_2_out, D, C);
  not not_1 (not_1_out, C);
  not not_2 (not_2_out, B);
  not not_3 (not_3_out, D);
  not not_4 (not_4_out, B);
  not not_5 (not_5_out, E);
  not not_6 (not_6_out, D);
  not not_7 (not_7_out, B);
  not not_8 (not_8_out, B);
  or or_1 (a4, and_1_out, and_2_out, E);
  and and_3 (and_3_out, D, not_1_out, not_2_out);
  and and_4 (and_4_out, E, B);
  and and_5 (and_5_out, not_3_out, C);
  and and_6 (and_6_out, C, B);
  and and_7 (and_7_out, E, not_4_out);
  and and_8 (and_8_out, not_5_out, not_6_out, B);
  and and_9 (and_9_out, D, C, not_7_out);
  and and_10 (and_10_out, E, not_8_out);
  or or_2 (a3, and_3_out, and_4_out);
  or or_3 (a2, and_5_out, and_6_out, and_7_out);
  or or_4 (a1, and_8_out, and_9_out, and_10_out);

  assign a0 = A;
endmodule

module AdderBCD (
  input  [3:0] in_1,
  input  [3:0] in_2
);

  wire adder_1_cout, bcdshow_1_a4;
  wire [3:0] adder_1_out, bcdshow_1_a0;

  Hex_Digit_Display hex_digit_display_1 (.value(in_1));  // open: dp
  Hex_Digit_Display hex_digit_display_2 (.value(in_2));  // open: dp
  Hex_Digit_Display hex_digit_display_3 (.value(adder_1_out));  // open: dp
  Adder #(.width(4)) adder_1 (.a(in_1), .b(in_2), .out(adder_1_out), .cin(1'b0), .cout(adder_1_cout));
  BCDshow bcdshow_1 (
    .E(adder_1_cout), .D(adder_1_out[3]), .C(adder_1_out[2]), .B(adder_1_out[1]), .A(adder_1_out[0]),
    .a4(bcdshow_1_a4), .a3(bcdshow_1_a0[3]), .a2(bcdshow_1_a0[2]), .a1(bcdshow_1_a0[1]), .a0(bcdshow_1_a0[0]));
  _7_Segment_Display u_7_segment_display_1 (.b(bcdshow_1_a4), .c(bcdshow_1_a4));  // open: g, f, a, e, d, dp
  Hex_Digit_Display hex_digit_display_4 (.value(bcdshow_1_a0));  // open: dp
endmodule

module BCD1Adder (
  input  in_1,
  input  [3:0] in_2,
  input  [3:0] in_3,
  output out_4,
  output [3:0] out_5
);

  wire adder_1_cout;
  wire [3:0] adder_1_out;

  Adder #(.width(4)) adder_1 (.a(in_2), .b(in_3), .out(adder_1_out), .cin(in_1), .cout(adder_1_cout));
  BCDshow bcdshow_1 (
    .E(adder_1_cout), .D(adder_1_out[3]), .C(adder_1_out[2]), .B(adder_1_out[1]), .A(adder_1_out[0]),
    .a4(out_4), .a3(out_5[3]), .a2(out_5[2]), .a1(out_5[1]), .a0(out_5[0]));
  _7_Segment_Display u_7_segment_display_1 (.b(out_4), .c(out_4));  // open: g, f, a, e, d, dp
  Hex_Digit_Display hex_digit_display_1 (.value(out_5));  // open: dp
endmodule

module BCD2Adder (
  input  [3:0] in_1,
  input  [3:0] in_2,
  input  [3:0] in_3,
  input  [3:0] in_4
);

  wire bcd1adder_1_out_4, bcd1adder_2_out_4;
  wire [3:0] bcd1adder_1_out_5, bcd1adder_2_out_5;

  Hex_Digit_Display hex_digit_display_1 (.value(in_1));  // open: dp
  Hex_Digit_Display hex_digit_display_2 (.value(in_3));  // open: dp
  _7_Segment_Display u_7_segment_display_1 (.b(bcd1adder_1_out_4), .c(bcd1adder_1_out_4));  // open: g, f, a, e, d, dp
  Hex_Digit_Display hex_digit_display_3 (.value(bcd1adder_1_out_5));  // open: dp
  Hex_Digit_Display hex_digit_display_4 (.value(in_2));  // open: dp
  Hex_Digit_Display hex_digit_display_5 (.value(in_4));  // open: dp
  Hex_Digit_Display hex_digit_display_6 (.value(bcd1adder_2_out_5));  // open: dp
  BCD1Adder bcd1adder_1 (
    .in_2(in_1), .in_3(in_3), .in_1(bcd1adder_2_out_4), .out_4(bcd1adder_1_out_4), .out_5(bcd1adder_1_out_5));
  BCD1Adder bcd1adder_2 (.in_2(in_2), .in_3(in_4), .in_1(1'b0), .out_4(bcd1adder_2_out_4), .out_5(bcd1adder_2_out_5));
endmodule
