// Logisim project 03-bitcont.circ as structural Verilog: 1 circuit, main circuit main
module main (
  input  [2:0] in_1
);

  wire bitselector_1_out, bitselector_2_out, bitselector_3_out;
  wire [1:0] adder_1_out, adder_2_out, bit_extender_1_out, bit_extender_2_out, bit_extender_3_out;
  wire [3:0] bit_extender_4_out;

  BitSelector #(.width(3)) bitselector_1 (.in(in_1), .out(bitselector_1_out), .sel(2'b00));
  BitSelector #(.width(3)) bitselector_2 (.in(in_1), .out(bitselector_2_out), .sel(2'b01));
  BitSelector #(.width(3)) bitselector_3 (.in(in_1), .out(bitselector_3_out), .sel(2'b10));
  assign bit_extender_1_out = {{1{1'b0}}, bitselector_1_out};  // Bit_Extender bit_extender_1
  assign bit_extender_2_out = {{1{1'b0}}, bitselector_2_out};  // Bit_Extender bit_extender_2
  assign bit_extender_3_out = {{1{1'b0}}, bitselector_3_out};  // Bit_Extender bit_extender_3
  Adder #(.width(2)) adder_1 (.a(bit_extender_1_out), .b(bit_extender_2_out), .out(adder_1_out));  // open: cin, cout
  Adder #(.width(2)) adder_2 (.a(adder_1_out), .b(bit_extender_3_out), .out(adder_2_out));  // open: cin, cout
  assign bit_extender_4_out = {{2{1'b0}}, adder_2_out};  // Bit_Extender bit_extender_4
  Hex_Digit_Display hex_digit_display_1 (.value(bit_extender_4_out));  // open: dp
endmodule
