// Logisim project 1.circ as structural Verilog: 2 circuits, main circuit main
module main (
  input  [3:0] in_1
);

  wire sub_1_a_2, sub_1_b_2, sub_1_c_2, sub_1_d_2, sub_1_e, sub_1_f, sub_1_g;

  Sub sub_1 (
    .A(in_1[3]), .B(in_1[2]), .C(in_1[1]), .D(in_1[0]), .A_2(sub_1_a_2), .B_2(sub_1_b_2), .C_2(sub_1_c_2),
    .D_2(sub_1_d_2), .E(sub_1_e), .F(sub_1_f), .G(sub_1_g));
  _7_Segment_Display u_7_segment_display_1 (
    .g(sub_1_g), .f(sub_1_f), .a(sub_1_a_2), .b(sub_1_b_2), .e(sub_1_e), .d(sub_1_d_2), .c(sub_1_c_2));  // open: dp
endmodule

module Sub (
  input  A,
  input  B,
  input  C,
  input  D,
  output A_2,
  output B_2,
  output C_2,
  output D_2,
  output E,
  output F,
  output G
);

  wire and_1_out, and_2_out, and_3_out, and_4_out, and_5_out, and_6_out, and_7_out, and_8_out, and_9_out,
       and_10_out, and_11_out, and_12_out, and_13_out, and_14_out, and_15_out, and_16_out, and_17_out,
       and_18_out, not_1_out, not_2_out, not_3_out, not_4_out, not_5_out, not_6_out, not_7_out, not_8_out,
       not_9_out, not_10_out, not_11_out, not_12_out, not_13_out, not_14_out, not_15_out, not_16_out,
       not_17_out, not_18_out, not_19_out, not_20_out, not_21_out, not_22_out, not_23_out, not_24_out;

  not not_1 (not_1_out, B);
  and and_1 (and_1_out, not_1_out, not_2_out);
  not not_2 (not_2_out, D);
  not not_3 (not_3_out, B);
  and and_2 (and_2_out, not_3_out, C);
  not not_4 (not_4_out, A);
  and and_3 (and_3_out, not_4_out, B, D);
  and and_4 (and_4_out, A, not_5_out);
  not not_5 (not_5_out, B);
  not not_6 (not_6_out, B);
  not not_7 (not_7_out, C);
  and and_5 (and_5_out, not_7_out, not_8_out);
  not not_8 (not_8_out, D);
  and and_6 (and_6_out, C, D);
  not not_9 (not_9_out, C);
  or or_1 (C_2, not_9_out, D, B);
  not not_10 (not_10_out, B);
  and and_7 (and_7_out, not_10_out, not_11_out);
  not not_11 (not_11_out, D);
  not not_12 (not_12_out, B);
  and and_8 (and_8_out, not_12_out, C);
  and and_9 (and_9_out, C, not_13_out);
  not not_13 (not_13_out, D);
  not not_14 (not_14_out, C);
  and and_10 (and_10_out, B, not_14_out, D);
  not not_15 (not_15_out, B);
  and and_11 (and_11_out, not_15_out, not_16_out);
  not not_16 (not_16_out, D);
  and and_12 (and_12_out, C, not_17_out);
  not not_17 (not_17_out, D);
  not not_18 (not_18_out, C);
  and and_13 (and_13_out, not_18_out, not_19_out);
  not not_19 (not_19_out, D);
  and and_14 (and_14_out, B, not_20_out);
  not not_20 (not_20_out, C);
  and and_15 (and_15_out, B, not_21_out);
  not not_21 (not_21_out, D);
  not not_22 (not_22_out, B);
  and and_16 (and_16_out, not_22_out, C);
  and and_17 (and_17_out, B, not_23_out);
  not not_23 (not_23_out, C);
  and and_18 (and_18_out, B, not_24_out);
  not not_24 (not_24_out, D);
  or or_2 (A_2, and_1_out, and_2_out, and_3_out, and_4_out);
  or or_3 (B_2, not_6_out, and_5_out, and_6_out);
  or or_4 (D_2, and_7_out, and_8_out, and_9_out, and_10_out);
  or or_5 (E, and_11_out, and_12_out);
  or or_6 (F, and_13_out, and_14_out, and_15_out, A);
  or or_7 (G, and_16_out, and_17_out, and_18_out, A);
endmodule
