// Logisim project 4.circ as structural Verilog: 1 circuit, main circuit main
module main (
  input  [7:0] in_1
);

  wire bitselector_1_out, bitselector_2_out, bitselector_3_out, bitselector_4_out, bitselector_5_out,
       bitselector_6_out, bitselector_7_out, bitselector_8_out;
  wire [3:0] adder_1_out, adder_2_out, adder_3_out, adder_4_out, adder_5_out, adder_6_out, adder_7_out,
       bit_extender_1_out, bit_extender_2_out, bit_extender_3_out, bit_extender_4_out, bit_extender_5_out,
       bit_extender_6_out, bit_extender_7_out, bit_extender_8_out;

  BitSelector bitselector_1 (.in(in_1), .out(bitselector_1_out), .sel(3'b000));
  BitSelector bitselector_2 (.in(in_1), .out(bitselector_2_out), .sel(3'b001));
  BitSelector bitselector_3 (.in(in_1), .out(bitselector_3_out), .sel(3'b010));
  BitSelector bitselector_4 (.in(in_1), .out(bitselector_4_out), .sel(3'b011));
  BitSelector bitselector_5 (.in(in_1), .out(bitselector_5_out), .sel(3'b100));
  BitSelector bitselector_6 (.in(in_1), .out(bitselector_6_out), .sel(3'b101));
  BitSelector bitselector_7 (.in(in_1), .out(bitselector_7_out), .sel(3'b110));
  BitSelector bitselector_8 (.in(in_1), .out(bitselector_8_out), .sel(3'b111));
  assign bit_extender_1_out = {{3{1'b0}}, bitselector_1_out};  // Bit_Extender bit_extender_1
  assign bit_extender_2_out = {{3{1'b0}}, bitselector_2_out};  // Bit_Extender bit_extender_2
  assign bit_extender_3_out = {{3{1'b0}}, bitselector_3_out};  // Bit_Extender bit_extender_3
  assign bit_extender_4_out = {{3{1'b0}}, bitselector_4_out};  // Bit_Extender bit_extender_4
  assign bit_extender_5_out = {{3{1'b0}}, bitselector_5_out};  // Bit_Extender bit_extender_5
  assign bit_extender_6_out = {{3{1'b0}}, bitselector_6_out};  // Bit_Extender bit_extender_6
  assign bit_extender_7_out = {{3{1'b0}}, bitselector_7_out};  // Bit_Extender bit_extender_7
  assign bit_extender_8_out = {{3{1'b0}}, bitselector_8_out};  // Bit_Extender bit_extender_8
  Adder #(.width(4)) adder_1 (.a(bit_extender_1_out), .b(bit_extender_2_out), .out(adder_1_out));  // open: cin, cout
  Adder #(.width(4)) adder_2 (.a(bit_extender_3_out), .b(bit_extender_4_out), .out(adder_2_out));  // open: cin, cout
  Adder #(.width(4)) adder_3 (.a(bit_extender_5_out), .b(bit_extender_6_out), .out(adder_3_out));  // open: cin, cout
  Adder #(.width(4)) adder_4 (.a(bit_extender_7_out), .b(bit_extender_8_out), .out(adder_4_out));  // open: cin, cout
  Adder #(.width(4)) adder_5 (.a(adder_3_out), .b(adder_4_out), .out(adder_5_out));  // open: cin, cout
  Adder #(.width(4)) adder_6 (.a(adder_1_out), .b(adder_2_out), .out(adder_6_out));  // open: cin, cout
  Adder #(.width(4)) adder_7 (.a(adder_6_out), .b(adder_5_out), .out(adder_7_out));  // open: cin, cout
  Hex_Digit_Display hex_digit_display_1 (.value(adder_7_out));  // open: dp
endmodule
